// Logisim project LMC.circ as structural Verilog: 4 circuits, main circuit Computer
// CTRL
module Control (
  input  [23:0] Input,
  input  [23:0] Read,
  input  [23:0] RES,
  input  in_4,
  input  Clock,
  output Input_Flag,
  output Write,
  output Output_Flag,
  output [15:0] Adress,
  output [23:0] Write_2,
  output [23:0] A,
  output [23:0] B,
  output [1:0] C,
  output [23:0] Output
);

  wire Acc_change, and_2_out, Clock_t, CT0, CT1, CT2, CT5, CT6, CT7, CT8, CT9, CT10, d_ff_1_qn, NeedJump,
       not_1_out, or_1_out, or_2_out, or_4_out;
  wire [1:0] Acc_input_chooser;
  wire [15:0] Command_Adress, Value_Adress;
  wire [23:0] multiplexer_2_out;
  wire [23:16] Command_Saver_q;

  Register #(.width(24)) Command_Saver (.D(Read), .Q({Command_Saver_q, Value_Adress}), .clk(Clock_t));  // open: en, clr
  D_Flip_Flop #(.trigger("falling")) d_ff_1 (.clk(Clock_t), .D(CT0), .Qn(d_ff_1_qn));  // open: Q, preset, en, reset
  and and_1 (Clock_t, d_ff_1_qn, Clock);
  not not_1 (not_1_out, NeedJump);
  Demultiplexer #(.select(4), .enable("false")) demultiplexer_1 (
    .out0(CT0), .out1(CT1), .out2(CT2), .out3(Write), .out5(CT5), .out6(CT6), .out7(CT7), .out8(CT8),
    .out9(CT9), .out10(CT10), .in(Clock_t), .sel(Command_Saver_q[23:20]));  // open: out4, out11, out12, out13, out14, out15
  Counter #(.width(16), .max('hffff), .trigger("falling")) counter_1 (
    .load(NeedJump), .D(Value_Adress), .count(not_1_out), .Q(Command_Adress), .clk(Clock_t));  // open: carry, clr
  Multiplexer #(.width(16), .enable("false")) multiplexer_1 (
    .in0(Command_Adress), .in1(Value_Adress), .out(Adress), .sel(Clock_t));
  or or_1 (or_1_out, CT8, CT7);
  and and_2 (and_2_out, in_4, or_1_out);
  Multiplexer #(.select(2), .width(24)) multiplexer_2 (
    .in1(Input), .in2(Read), .in3(RES), .out(multiplexer_2_out), .sel(Acc_input_chooser));  // open: in0, en
  Register #(.width(24), .trigger("falling")) register_1 (
    .D(multiplexer_2_out), .Q(A), .clk(Acc_change));  // open: en, clr
  or or_2 (or_2_out, CT1, CT2, CT5, CT9);
  assign Acc_change = or_2_out ? Clock_t : 1'bz;  // Controlled_Buffer controlled_buffer_1
  or or_3 (NeedJump, and_2_out, CT6);
  assign Input_Flag = CT9 ? Clock_t : 1'bz;  // Controlled_Buffer controlled_buffer_2
  Choooser choooser_1 (._0(CT1), ._1(CT2), ._2(CT7), ._3(CT8), .Number_of_enter__where_1(C));
  or or_4 (or_4_out, CT2, CT1);
  Choooser choooser_2 (._1(CT9), ._2(CT5), ._3(or_4_out), .Number_of_enter__where_1(Acc_input_chooser));  // open: _0
  and and_3 (Output_Flag, Clock_t, CT10);
  assign Output = Output_Flag ? A : 24'bz;  // Controlled_Buffer controlled_buffer_3

  assign B = Read;
  assign Write_2 = A;

  // Other names for the same wires on the sheet: ALU_b[23:0] = Read; ALU_LOut = in_4; ALU_mode[1:0] = C;
  //   ALU_out[23:0] = RES; ClockIN = Clock; HLT = CT0; Accumulator_Data[23:0] = A; ALU_a[23:0] = A; Write_t[23:0] = A;
  //   CT3 = Write; WriteMod = Write

  // Notes on the sheet:
  //   Outside control
  //   CLOCK IN SCHEME AND HLT
  //   RAM
  //   Command Chooser
  //   Command decoder
  //   Adress Chooser
  //   ALU
  //   Command 0
  //   Command 3
  //   Accumulator
  //   Output
  //   Accumaltor change flag
  //   Jump
  //   Input Flag
  //   Setting ALU inputs
  //   Accumaltor input choose
  //   Command 9_2
endmodule

// CH
module Choooser (
  input  _0,
  input  _1,
  input  _2,
  input  _3,
  output [1:0] Number_of_enter__where_1
);

  or or_1 (Number_of_enter__where_1[0], _1, _3);
  or or_2 (Number_of_enter__where_1[1], _2, _3);
endmodule

module ALU (
  input  [23:0] a,
  input  [23:0] b,
  input  [1:0] c,
  output [23:0] Out,
  output Lout
);

  wire comparator_1_eq, comparator_1_lt, not_1_out;
  wire [23:0] adder_1_out, bit_extender_1_out, bit_extender_2_out, subtractor_1_out;

  Adder #(.width(24)) adder_1 (.a(a), .b(b), .out(adder_1_out));  // open: cin, cout
  Subtractor #(.width(24)) subtractor_1 (.a(a), .b(b), .out(subtractor_1_out));  // open: bin, bout
  Comparator #(.width(24)) comparator_1 (
    .a(a), .b({24{1'b0}}), .eq(comparator_1_eq), .lt(comparator_1_lt));  // open: gt
  assign bit_extender_1_out = {{23{1'b0}}, comparator_1_eq};  // Bit_Extender bit_extender_1
  not not_1 (not_1_out, comparator_1_lt);
  assign bit_extender_2_out = {{23{1'b0}}, not_1_out};  // Bit_Extender bit_extender_2
  Multiplexer #(.select(2), .width(24), .enable("false")) multiplexer_1 (
    .in0(adder_1_out), .in1(subtractor_1_out), .in2(bit_extender_1_out), .in3(bit_extender_2_out), .out(Out),
    .sel(c));
  Bit_Extender #(.in_width(24), .out_width(1)) bit_extender_3 (.in(Out), .out(Lout));

  // Other names for the same wires on the sheet: RES[23:0] = Out

  // Notes on the sheet:
  //   Input
  //   Main Part
  //   Output
endmodule

module Computer (
  input  [23:0] _0,
  input  [23:0] _1,
  input  [23:0] _2,
  input  [23:0] _3,
  input  [23:0] _4,
  input  [23:0] _5,
  input  [23:0] _6,
  input  [23:0] _7
);

  wire alu_1_lout, clock_1_out, control_1_input_flag, control_1_output_flag, control_1_write;
  wire [1:0] control_1_c;
  wire [2:0] counter_1_q;
  wire [15:0] control_1_adress;
  wire [23:0] alu_1_out, control_1_a, control_1_b, control_1_output, control_1_write_2, multiplexer_1_out,
       ram_1_data, register_1_q;

  Counter #(.width(3), .max('h7), .trigger("falling")) counter_1 (
    .Q(counter_1_q), .clk(control_1_input_flag));  // open: load, D, count, carry, clr
  Multiplexer #(.select(3), .width(24), .enable("false")) multiplexer_1 (
    .in0(_0), .in1(_1), .in2(_2), .in3(_3), .in4(_4), .in5(_5), .in6(_6), .in7(_7), .out(multiplexer_1_out),
    .sel(counter_1_q));
  Clock clock_1 (.out(clock_1_out));
  RAM #(.addrWidth(16), .dataWidth(24), .bus("separate")) ram_1 (
    .addr(control_1_adress), .din(control_1_write_2), .data(ram_1_data), .clk(control_1_write));  // open: str, sel, ld, clr
  ALU alu_1 (.a(control_1_a), .b(control_1_b), .c(control_1_c), .Out(alu_1_out), .Lout(alu_1_lout));
  Control control_1 (
    .Input_Flag(control_1_input_flag), .Input(multiplexer_1_out), .Clock(clock_1_out), .Read(ram_1_data),
    .Write_2(control_1_write_2), .Adress(control_1_adress), .Write(control_1_write), .RES(alu_1_out),
    .in_4(alu_1_lout), .A(control_1_a), .B(control_1_b), .C(control_1_c),
    .Output_Flag(control_1_output_flag), .Output(control_1_output));
  Register #(.width(24), .trigger("high")) register_1 (
    .D(control_1_output), .Q(register_1_q), .clk(control_1_output_flag));  // open: en, clr
  // Probe on register_1_q
  LED led_1 (.in(control_1_output_flag));

  // Notes on the sheet:
  //   input queue
endmodule
